// Logisim project aac.circ as structural Verilog: 2 circuits, main circuit aaaa
module aaaa (
  input  in_1,
  input  [2:0] in_2
);

  wire [5:0] demux_1_out_3, demux_1_out_4, demux_1_out_5, demux_1_out_6, demux_1_out_7;

  demux demux_1 (
    .in_1(in_1), .in_2(in_2), .out_3(demux_1_out_3), .out_4(demux_1_out_4), .out_5(demux_1_out_5),
    .out_6(demux_1_out_6), .out_7(demux_1_out_7));
  DotMatrix #(.matrixcols(7), .matrixrows(6)) dotmatrix_1 (
    .col1(demux_1_out_3), .col2(demux_1_out_4), .col3(demux_1_out_5), .col4(demux_1_out_6),
    .col5(demux_1_out_7));  // open: col0, col6
endmodule

module demux (
  input  in_1,
  input  [2:0] in_2,
  output [5:0] out_3,
  output [5:0] out_4,
  output [5:0] out_5,
  output [5:0] out_6,
  output [5:0] out_7
);

  wire demultiplexer_1_out0, demultiplexer_1_out1, demultiplexer_1_out2, demultiplexer_1_out3,
       demultiplexer_1_out4;

  Demultiplexer #(.select(3), .enable("false")) demultiplexer_1 (
    .out0(demultiplexer_1_out0), .out1(demultiplexer_1_out1), .out2(demultiplexer_1_out2),
    .out3(demultiplexer_1_out3), .out4(demultiplexer_1_out4), .in(in_1), .sel(in_2));  // open: out5, out6, out7
  or or_1 (out_3[1], demultiplexer_1_out3, demultiplexer_1_out4);
  or or_2 (out_3[2], demultiplexer_1_out0, demultiplexer_1_out1);
  or or_3 (out_4[4], demultiplexer_1_out0, demultiplexer_1_out1, demultiplexer_1_out2, demultiplexer_1_out3, demultiplexer_1_out4);
  or or_4 (out_4[2], demultiplexer_1_out0, demultiplexer_1_out3, demultiplexer_1_out4);
  or or_5 (out_4[1], demultiplexer_1_out0, demultiplexer_1_out1, demultiplexer_1_out2);
  or or_6 (out_5[2], demultiplexer_1_out0, demultiplexer_1_out3);
  or or_7 (out_5[1], demultiplexer_1_out0, demultiplexer_1_out1, demultiplexer_1_out2, demultiplexer_1_out4);
  or or_8 (out_6[4], demultiplexer_1_out0, demultiplexer_1_out1, demultiplexer_1_out2, demultiplexer_1_out3, demultiplexer_1_out4);
  or or_9 (out_6[2], demultiplexer_1_out0, demultiplexer_1_out3, demultiplexer_1_out4);
  or or_10 (out_6[1], demultiplexer_1_out0, demultiplexer_1_out1, demultiplexer_1_out2);
  or or_11 (out_7[1], demultiplexer_1_out3, demultiplexer_1_out4);
  or or_12 (out_7[2], demultiplexer_1_out0, demultiplexer_1_out1);

  assign {out_3[5:3], out_3[0]} = 4'b0000;
  assign {out_4[5], out_4[3], out_4[0]} = 3'b000;
  assign {out_5[5:3], out_5[0]} = 4'b0000;
  assign {out_6[5], out_6[3], out_6[0]} = 3'b000;
  assign {out_7[5:3], out_7[0]} = 4'b0000;
endmodule
